# Fritzing sketch Untitled Sketch (saved by Fritzing 0.9.3b)
breadboards: 2

parts:
  U1 = LM 358 Dual Op-Amp [package="DIP8 [THT]"]
  R1 = Resistor [tolerance=±5% resistance=10k package=THT]
  R2 = Resistor [tolerance=±5% resistance=10k package=THT]
  J1 = Basic Force Sensing Resistor (FSR) [package=THT]
  J2 = Basic Force Sensing Resistor (FSR) [package=THT]
  Raspberry_Pi_1 = Raspberry Pi 3 [part_number=RPI-3-V1.2]
  D1 = LED_BARGRAPH_10 [package=led_bargaph_10]
  R3 = Resistor [tolerance=±5% resistance=220 package=THT]

nets:
  N1: U1.connector0, Raspberry_Pi_1.GPIO10
  N2: U1.connector1, Raspberry_Pi_1.GPIO9
  N3: U1.connector2, Raspberry_Pi_1.GPIO11
  N4: U1.connector3, J1.pin_0, J2.pin_1, Raspberry_Pi_1.3v3
  N5: U1.connector4, Raspberry_Pi_1.GPIO8
  N6: U1.connector5, R1.Pin_1, J1.pin_1
  N7: U1.connector6, R2.Pin_1, J2.pin_0
  N8: U1.connector7, R1.Pin_0, R2.Pin_0, Raspberry_Pi_1.GND, R3.Pin_1
  N9: Raspberry_Pi_1.GPIO17, D1.A_A
  N10: Raspberry_Pi_1.GPIO27, D1.B_A
  N11: Raspberry_Pi_1.GPIO22, D1.C_A
  N12: Raspberry_Pi_1.GPIO5, D1.F_A
  N13: Raspberry_Pi_1.GPIO6, D1.G_A
  N14: Raspberry_Pi_1.GPIO13, D1.H_A
  N15: Raspberry_Pi_1.GPIO19, D1.I_A
  N16: Raspberry_Pi_1.GPIO26, D1.J_A
  N17: Raspberry_Pi_1.GPIO24, D1.E_A
  N18: Raspberry_Pi_1.GPIO23, D1.D_A
  N19: D1.J_C, D1.I_C, D1.H_C, D1.G_C, D1.F_C, D1.E_C, D1.D_C, D1.C_C, D1.B_C, D1.A_C, R3.Pin_0
